# Fritzing sketch circuit sketch (saved by Fritzing 1.0.6)
circuit board: 8.46667cm x 5.64444cm
breadboards: 1

parts:
  Mod1 = Raspberry Pi Pico
  Part1 = OLED Monochrome 128x64 1.3 inch [part_number=938]
  ENCODER1 = Rotary Encoder with Knob
  LED1 = LED - 5mm [color="Green (565nm)" current=0.030A package="5 mm [THT]"]
  LED2 = LED - 5mm [color="Red (633nm)" current=0.030A package="5 mm [THT]"]
  LED3 = LED - 5mm [color="White (4500K)" current=0.030A package="5 mm [THT]"]
  R1 = Resistor [tolerance=±5% power=0.25W resistance=330 package=THT]
  R2 = Resistor [tolerance=±5% power=0.25W resistance=330 package=THT]
  R3 = Resistor [tolerance=±5% power=0.25W resistance=330 package=THT]

nets:
  N1: Mod1.pin_1, Part1.MOSI_SDA
  N2: Mod1.pin_2, Part1.SCLK_SCK
  GND: Mod1.pin_3, Mod1.pin_8, Mod1.pin_13, Mod1.pin_18, Mod1.pin_23, Mod1.pin_28, Mod1.pin_33, Mod1.pin_38, Part1.GND, ENCODER1.no_name_yet#3, ENCODER1.no_name_yet#5, LED1.cathode, LED2.cathode, LED3.cathode
  N3: Mod1.pin_4, ENCODER1.no_name_yet#1
  N4: Mod1.pin_5, ENCODER1.no_name_yet#2
  N5: Mod1.pin_14, R2.Pin_1
  N6: Mod1.pin_15, R3.Pin_1
  N7: Mod1.pin_16, R1.Pin_1
  N8: Mod1.pin_20, ENCODER1.no_name_yet#4
  3.3V: Mod1.pin_36, Part1.3.3V
  N9: LED1.anode, R2.Pin_0
  N10: LED2.anode, R1.Pin_0
  N11: LED3.anode, R3.Pin_0

custom parts:
  Raspberry Pi Pico: Raspberry Pi Pico. Based around the RP2040 microcontroller the Pico is a low cost microcontroller device bringing Raspberry Pi quality, cost, and easy of use to the microcontroller space. Jan 2021, Split part in to two versions: SMD (this one) and tht. This one is single sided and uses the castellation pads to solder the module to the board (no holes, other than for the USB connector!). The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
  OLED Monochrome 128x64 1.3 inch: These displays are small, only about 1.3" diagonal, but very readable due to the high contrast of an OLED display. This display is made of 128x64 individual white OLED pixels, each one is turned on or off by the controller chip. Because the display makes its own light, no backlight is required. This reduces the power required to run the OLED and is why the display has such high contrast; we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
  Rotary Encoder with Knob: Rotary Encoder with 1/4" Shaft and Knob
